# Fritzing sketch BVM 1st Circuit (saved by Fritzing 0.9.6b)
perfboards: 1

parts:
  Part1 = Arduino Nano (Rev3.0)
  J1 = Piezo Speaker
  VCC1 = Battery
  Part3 = Mono 2.5W Class D Audio Amplifier - PAM8302
  OLED1 = WaveShare 1.3 inch OLED
  J8 = female pin header, 2 pins [form="♀ (female)"]
  J6 = female pin header, 2 pins [form="♀ (female)"]
  S1 = Pushbutton [package=THT]
  R1 = Resistor [tolerance=±5% power=0.25 resistance=220 package=THT]

nets:
  N1: Part1.GND, VCC1.-, Part3.AIN-, J6.pin1
  N2: Part1.D5, R1.Pin_1
  N3: Part1.D7, OLED1.D/C
  N4: Part1.D8, OLED1.RES
  N5: Part1.D10, OLED1.CS
  N6: Part1.D11/MOSI, OLED1.DIN
  5V: Part1.5V, Part3.VCC, J8.pin2, S1.leg0
  N7: Part1.D13/SCK, OLED1.CLK
  N8: J1.pin1, Part3.VO+
  N9: J1.pin2, Part3.VO-
  N10: VCC1.+, S1.leg1
  N11: Part3.GND, J8.pin1
  N12: Part3.AIN+, J6.pin2, R1.Pin_0

notes:
  The Flow Sensor Would Go here
  Need to Verify the Resistance, am unsure what it is

custom parts:
  Mono 2.5W Class D Audio Amplifier - PAM8302: A super small but powerful mono amplifier able to deliver up to 2.5 Watts into 4-8 ohm impedance speakers. Inside the miniature chip is a class D controller, able to run from 2.0V-5.5VDC. Since the amp is a class D, its very efficient (over 90% efficient when driving an 8Ω speaker at over half a Watt) - making it perfect for portable and battery-powered projects.
  WaveShare 1.3 inch OLED: 128x64 Monochrom OLED Display with a SH1106 controller
