# Fritzing sketch BVM Future Circuit (saved by Fritzing 0.9.6b)
perfboards: 1

parts:
  J1 = female pin header, 2 pins [form="♀ (female)"]
  JACK1 = 2.1mm Barrel Jack with Terminal Block
  Part2 = Arduino Nano (Rev3.0)
  J2 = female pin header, 2 pins [form="♀ (female)"]
  J3 = female pin header, 2 pins [form="♀ (female)"]
  J4 = female pin header, 2 pins [form="♀ (female)"]
  R1 = Resistor [tolerance=±5% resistance=220 package="2010 [SMD]"]
  J5 = female pin header, 2 pins [form="♀ (female)"]
  J6 = female pin header, 2 pins [form="♀ (female)"]
  J7 = female pin header, 2 pins [form="♀ (female)"]
  J8 = female pin header, 2 pins [form="♀ (female)"]

nets:
  N1: J1.pin1, JACK1.NEG, Part2.GND, J2.pin1, J4.pin1, J5.pin1
  N2: J1.pin2, Part2.5V, J3.pin1, J5.pin2
  N3: JACK1.POS, Part2.VIN
  N4: Part2.D5, R1.Pin_1
  N5: Part2.D7, J8.pin2
  N6: Part2.D8, J7.pin1
  N7: Part2.D10, J7.pin2
  N8: Part2.D11/MOSI, J6.pin1
  N9: Part2.A5, J3.pin2
  N10: Part2.A4, J2.pin2
  N11: Part2.D13/SCK, J6.pin2
  N12: J4.pin2, R1.Pin_0

notes:
  Screen Connects Here, from right to left: Power, Ground, D13 to SCK, D11 to MISO, D10 to CS, D8 to RST, D7 to D/C
  Speaker Connects Here, from right to left: D5 through 100K Resister, Ground, Power, Ground
  Flow Sensor Connects Here, from right to left: A4 to Data, Ground, A5 to SCK, Power
